// Logisim project sCPU.circ as structural Verilog: 1 circuit, main circuit main
module main (
);

  Adder adder_1 ();  // open: a, b, out, cin, cout
  // AND_Gate and_1 is placed but not wired
  Register #(.width(4)) PC ();  // open: D, en, clk, Q, clr
  // OR_Gate or_1 is placed but not wired
endmodule
